# Fritzing sketch MPU6050 (WEMOS - Deprecated)-diagram (saved by Fritzing 0.9.10b)
breadboards: 1

parts:
  Part1 = InvenSense MPU6050
  WeMos_D1_Mini1 = WeMos D1 Mini

nets:
  VCC: Part1.VCC, WeMos_D1_Mini1.3V3
  N1: Part1.GND, WeMos_D1_Mini1.G
  N2: Part1.SCL, WeMos_D1_Mini1.D1
  N3: Part1.SDA, WeMos_D1_Mini1.D2
