# Fritzing sketch PROJECT-diagram (saved by Fritzing 0.9.10b)
breadboards: 2

parts:
  Part1 = InvenSense MPU6050
  M1 = ESP32-S3-DevKitC-1-N8R8-v1 [part_number=ESP32-S3-DevKitC-1-N8R8-v1]
  M2 = ESP32-S3-DevKitC-1-N8R8-v1 [part_number=ESP32-S3-DevKitC-1-N8R8-v1]

nets:
  N1: Part1.VCC, M1.pin_1, M1.pin_2, M2.pin_1, M2.pin_2
  N2: Part1.GND, M1.pin_22, M1.pin_23, M1.pin_24, M1.pin_44, M2.pin_22, M2.pin_23, M2.pin_24, M2.pin_44
  N3: Part1.SCL, M1.pin_16
  N4: Part1.SDA, M1.pin_13

custom parts:
  ESP32-S3-DevKitC-1-N8R8-v1: ESP32-S3-DevKitC-1-N8R8-v1 This module is 44pins long (2x22) and 11 pins width.
